// Logisim project 3lab.circ as structural Verilog: 6 circuits, main circuit main
module main (
  input  X2,
  input  X1,
  input  X0,
  output [7:0] out_4,
  output Y7,
  output Y6,
  output Y5,
  output Y4,
  output Y3,
  output Y2,
  output Y1,
  output Y0,
  output \Don_t_care_нет_нулей ,
  output Z1,
  output Z0,
  output [7:0] out_16,
  output Y7_2,
  output Y6_2,
  output Y5_2,
  output Y4_2,
  output Y3_2,
  output Y2_2,
  output Y1_2,
  output Y0_2,
  output Don_t_care,
  output Z1_2,
  output Z0_2
);

  \Факториал_21_с_округлением  \u_факториал_21_с_округлением_1  (
    .X2(X2), .X1(X1), .X0(X0), .Y7(out_4[7]), .Y6(out_4[6]), .Y5(out_4[5]), .Y4(out_4[4]), .Y3(out_4[3]),
    .Y2(out_4[2]), .Y1(out_4[1]), .Y0(out_4[0]));
  // Probe on {X2, X1, X0}
  \Самый_младший__0__вход  \u_самый_младший_0_вход_1  (
    .X2(X2), .X1(X1), .X0(X0), .Z1(Z1), .Z0(Z0), .Don_t_care(\Don_t_care_нет_нулей ));
  \Факториал_21_с_округлением_с__don_t_care  \u_факториал_21_с_округлением_с_don_t_care_1  (
    .X2(X2), .X1(X1), .X0(X0), .Y7(out_16[7]), .Y6(out_16[6]), .Y5(out_16[5]), .Y4(out_16[4]),
    .Y3(out_16[3]), .Y2(out_16[2]), .Y1(out_16[1]), .Y0(out_16[0]), .Don_t_care(Don_t_care));
  \Самый_младший__0__вход_c__don_t_care  \u_самый_младший_0_вход_c_don_t_care_1  (
    .X2(X2), .X1(X1), .X0(X0), .Z1(Z1_2), .Z0(Z0_2), .Don_t_care(Don_t_care));
  // Probe on out_4
  // Probe on out_16

  assign Y0 = out_4[0];
  assign Y0_2 = out_16[0];
  assign Y1 = out_4[1];
  assign Y1_2 = out_16[1];
  assign Y2 = out_4[2];
  assign Y2_2 = out_16[2];
  assign Y3 = out_4[3];
  assign Y3_2 = out_16[3];
  assign Y4 = out_4[4];
  assign Y4_2 = out_16[4];
  assign Y5 = out_4[5];
  assign Y5_2 = out_16[5];
  assign Y6 = out_4[6];
  assign Y6_2 = out_16[6];
  assign Y7 = out_4[7];
  assign Y7_2 = out_16[7];

  // Notes on the sheet:
  //   Факториал/21 с округлением
  //   Самый младший "0" вход
  //   Факториал/21 с округлением
  //   Самый младший "0" вход
endmodule

module \Факториал_21_с_округлением_с__don_t_care  (
  input  X2,
  input  X1,
  input  X0,
  output Y7,
  output Y6,
  output Y5,
  output Y4,
  output Y3,
  output Y2,
  output Y1,
  output Y0,
  output Don_t_care
);

  wire and_1_out, and_7_out, and_8_out, controlled_buffer_1_out, controlled_buffer_2_out,
       controlled_buffer_3_out, nor_1_out, nor_2_out, not_1_out, not_2_out, not_3_out, not_4_out, not_5_out,
       not_6_out;

  and and_1 (and_1_out, X0, X1, X2);
  nor nor_1 (nor_1_out, X0, X1, X2);
  nor nor_2 (nor_2_out, and_1_out, nor_1_out);
  or or_1 (Don_t_care, nor_1_out, and_1_out);
  assign controlled_buffer_1_out = nor_2_out ? X0 : 1'bz;  // Controlled_Buffer controlled_buffer_1
  assign controlled_buffer_2_out = nor_2_out ? X2 : 1'bz;  // Controlled_Buffer controlled_buffer_2
  assign controlled_buffer_3_out = nor_2_out ? X1 : 1'bz;  // Controlled_Buffer controlled_buffer_3
  and and_2 (Y7, controlled_buffer_2_out, controlled_buffer_3_out, controlled_buffer_1_out);
  and and_3 (Y6, controlled_buffer_2_out, controlled_buffer_3_out, controlled_buffer_1_out);
  and and_4 (Y5, controlled_buffer_2_out, controlled_buffer_3_out);
  and and_5 (Y4, controlled_buffer_2_out, controlled_buffer_3_out, controlled_buffer_1_out);
  not not_1 (not_1_out, controlled_buffer_2_out);
  not not_2 (not_2_out, controlled_buffer_3_out);
  and and_6 (Y2, controlled_buffer_2_out, not_2_out, controlled_buffer_1_out);
  not not_3 (not_3_out, controlled_buffer_3_out);
  and and_7 (and_7_out, controlled_buffer_2_out, not_3_out, controlled_buffer_1_out);
  and and_8 (and_8_out, controlled_buffer_2_out, controlled_buffer_3_out, not_4_out);
  not not_4 (not_4_out, controlled_buffer_1_out);
  and and_9 (Y0, controlled_buffer_2_out, not_5_out, not_6_out);
  not not_5 (not_5_out, controlled_buffer_3_out);
  not not_6 (not_6_out, controlled_buffer_1_out);
  and and_10 (Y3, controlled_buffer_2_out, not_1_out);
  or or_2 (Y1, and_7_out, and_8_out);
endmodule

module \Самый_младший__0__вход_c__don_t_care  (
  input  X2,
  input  X1,
  input  X0,
  output Z1,
  output Z0,
  output Don_t_care
);

  wire and_1_out, controlled_buffer_2_out, controlled_buffer_3_out, nor_1_out, nor_2_out, not_1_out;

  and and_1 (and_1_out, X0, X1, X2);
  nor nor_1 (nor_1_out, and_1_out, nor_2_out);
  nor nor_2 (nor_2_out, X0, X1, X2);
  or or_1 (Don_t_care, nor_2_out, and_1_out);
  Controlled_Buffer controlled_buffer_1 (.in(X2), .en(nor_1_out));  // open: out
  assign controlled_buffer_2_out = nor_1_out ? X1 : 1'bz;  // Controlled_Buffer controlled_buffer_2
  assign controlled_buffer_3_out = nor_1_out ? X0 : 1'bz;  // Controlled_Buffer controlled_buffer_3
  and and_2 (Z1, controlled_buffer_2_out, controlled_buffer_3_out);
  not not_1 (not_1_out, controlled_buffer_2_out);
  and and_3 (Z0, controlled_buffer_3_out, not_1_out);
endmodule

module \Факториал_21_с_округлением  (
  input  X2,
  input  X1,
  input  X0,
  output Y7,
  output Y6,
  output Y5,
  output Y4,
  output Y3,
  output Y2,
  output Y1,
  output Y0
);

  wire and_7_out, and_8_out, not_1_out, not_2_out, not_3_out, not_4_out, not_5_out, not_6_out;

  and and_1 (Y7, X2, X1, X0);
  and and_2 (Y6, X2, X1, X0);
  and and_3 (Y5, X2, X1);
  and and_4 (Y4, X2, X1, X0);
  and and_5 (Y3, X2, not_1_out);
  not not_1 (not_1_out, X2);
  not not_2 (not_2_out, X1);
  and and_6 (Y2, X2, not_2_out, X0);
  not not_3 (not_3_out, X1);
  and and_7 (and_7_out, X2, not_3_out, X0);
  and and_8 (and_8_out, X2, X1, not_4_out);
  not not_4 (not_4_out, X0);
  and and_9 (Y0, X2, not_5_out, not_6_out);
  not not_5 (not_5_out, X1);
  not not_6 (not_6_out, X0);
  or or_1 (Y1, and_7_out, and_8_out);
endmodule

module \Самый_младший__0__вход  (
  input  X2,
  input  X1,
  input  X0,
  output Z1,
  output Z0,
  output Don_t_care
);

  wire controlled_buffer_1_out, controlled_buffer_2_out, controlled_buffer_3_out, not_1_out, not_2_out,
       not_3_out;

  and and_1 (Don_t_care, X0, X1, X2);
  not not_1 (not_1_out, Don_t_care);
  assign controlled_buffer_1_out = not_1_out ? X2 : 1'bz;  // Controlled_Buffer controlled_buffer_1
  assign controlled_buffer_2_out = not_1_out ? X1 : 1'bz;  // Controlled_Buffer controlled_buffer_2
  assign controlled_buffer_3_out = not_1_out ? X0 : 1'bz;  // Controlled_Buffer controlled_buffer_3
  not not_2 (not_2_out, controlled_buffer_1_out);
  and and_2 (Z1, not_2_out, controlled_buffer_2_out, controlled_buffer_3_out);
  not not_3 (not_3_out, controlled_buffer_2_out);
  and and_3 (Z0, controlled_buffer_3_out, not_3_out);
endmodule

module test (
  input  X2,
  input  X1,
  input  X0,
  input  X2_2,
  input  X1_2,
  input  X0_2,
  output Z1,
  output Z0,
  output Dont_care,
  output Z1_2,
  output Z0_2,
  output Dont_care_2
);

  wire _1_out, _2_out, not_1_out, not_2_out, undriven, undriven_2, undriven_3, undriven_4, undriven_5,
       undriven_6, undriven_7;

  not not_1 (not_1_out, X2);
  not not_2 (not_2_out, X1);
  and and_1 (Dont_care, X0, X1, X2);
  and and_2 (Z1, not_1_out, X1, X0);
  and and_3 (Z0, X0, not_2_out);
  not _2 (_2_out, undriven);
  not _1 (_1_out, undriven_2);
  and and_4 (Dont_care_2, undriven_3, undriven_4);
  and and_5 (Z1_2, _2_out, undriven_5, undriven_6);
  and and_6 (Z0_2, undriven_7, _1_out);

  // Notes on the sheet:
  //   0
endmodule
